# Fritzing sketch Fade (saved by Fritzing 0.9.3b)
breadboards: 1

parts:
  R1 = Resistor [tolerance=±5% resistance=220 package=THT]
  LED1 = LED - 5mm [color="Red (633nm)" package="5 mm [THT]"]
  Part1 = Arduino Uno (Rev3)

nets:
  N1: R1.Pin_0, Part1.D9_PWM
  N2: R1.Pin_1, LED1.cathode
  N3: LED1.anode, Part1.5V

// code stored in the sketch: fade.ino


int led = 9;          // the  pulse width modulation(PWM) pin the LED is attached to
int brightness = 0;   // how bright the LED is
int fadeAmount = 5;   // how many points to fade the LED by

// the setup routine runs once when you press reset:
void setup() {
    // declare pin 9 to be an output:
    pinMode(led, OUTPUT);
}

// the loop routine runs over and over again forever:
void loop() {
    // set the brightness of pin 9:
    analogWrite(led, brightness);

    // change the brightness for next time through the loop:
    brightness += fadeAmount;

    // reverse the direction of the fading at the end of the fade:
    if ( (brightness <= 0) || (brightness >= 255) )
        fadeAmount = -fadeAmount;
    // wait for 30 miliseconds to see the dimming effect
    delay(30);
}
